// Logisim project Operations of 4-bit.circ as structural Verilog: 1 circuit, main circuit main
module main (
  input  [3:0] in_1,
  input  [3:0] in_2,
  input  [3:0] in_3,
  input  in_4,
  input  [3:0] in_5,
  input  in_6,
  output [3:0] out_7,
  output out_8,
  output out_9,
  output [3:0] out_10,
  output A_B,
  output A_B_2,
  output A_B_3,
  output A__B,
  output A__B_2,
  output A_B_4,
  output A_B_5,
  output A__B_3,
  output A__B_4,
  output out_20,
  output A_B_6,
  output A__B_5,
  output A__B_6,
  output A_B_7,
  output A__B_7,
  output A__B_8,
  output A_B_8,
  output A_B_9,
  output A_B_10,
  output A_B_11
);

  wire and_1_out, and_2_out, and_3_out, and_4_out, and_5_out, and_6_out, and_7_out, and_8_out, and_9_out,
       and_10_out, and_13_out, and_14_out, and_15_out, and_16_out, and_20_out, and_21_out, and_23_out,
       and_24_out, clock_1_out, d_ff_1_q, d_ff_2_q, d_ff_3_q, d_ff_4_q, d_ff_5_q, d_ff_6_q, d_ff_7_q,
       d_ff_8_q, not_1_out, not_2_out, not_3_out, not_4_out, not_5_out, not_6_out, not_7_out, not_8_out,
       not_9_out, not_10_out, not_11_out, not_12_out, not_13_out, or_2_out, or_3_out, or_4_out, or_9_out,
       or_10_out, or_12_out, xor_1_out, xor_2_out, xor_7_out, xor_8_out, xor_9_out, xor_10_out, xor_15_out,
       xor_16_out;

  not not_1 (not_1_out, in_1[1]);
  not not_2 (not_2_out, in_1[2]);
  and and_1 (and_1_out, in_1[3], not_2_out, not_1_out, not_5_out);
  and and_2 (and_2_out, in_5[3], not_4_out, not_3_out, in_5[0]);
  not not_3 (not_3_out, in_5[1]);
  not not_4 (not_4_out, in_5[2]);
  not not_5 (not_5_out, in_1[0]);
  D_Flip_Flop d_ff_1 (.clk(clock_1_out), .D(in_2[3]), .Q(d_ff_1_q), .en(and_1_out));  // open: Qn, preset, reset
  xor xor_1 (xor_1_out, d_ff_5_q, d_ff_1_q);
  and and_3 (and_3_out, d_ff_5_q, d_ff_1_q);
  xor xor_2 (xor_2_out, d_ff_8_q, d_ff_4_q);
  and and_4 (and_4_out, d_ff_8_q, d_ff_4_q);
  D_Flip_Flop d_ff_2 (.clk(clock_1_out), .D(in_2[2]), .Q(d_ff_2_q), .en(and_1_out));  // open: Qn, preset, reset
  and and_5 (and_5_out, xor_1_out, or_3_out);
  and and_6 (and_6_out, xor_2_out, in_6);
  D_Flip_Flop d_ff_3 (.clk(clock_1_out), .D(in_2[1]), .Q(d_ff_3_q), .en(and_1_out));  // open: Qn, preset, reset
  or or_1 (out_9, and_5_out, and_3_out);
  or or_2 (or_2_out, and_6_out, and_4_out);
  Clock clock_1 (.out(clock_1_out));
  D_Flip_Flop d_ff_4 (.clk(clock_1_out), .D(in_2[0]), .Q(d_ff_4_q), .en(and_1_out));  // open: Qn, preset, reset
  xor xor_3 (out_10[3], xor_1_out, or_3_out);
  xor xor_4 (out_10[0], xor_2_out, in_6);
  xor xor_5 (out_10[2], xor_7_out, or_4_out);
  or or_3 (or_3_out, and_7_out, and_9_out);
  D_Flip_Flop d_ff_5 (.clk(clock_1_out), .D(in_3[3]), .Q(d_ff_5_q), .en(and_2_out));  // open: Qn, preset, reset
  and and_7 (and_7_out, xor_7_out, or_4_out);
  xor xor_6 (out_10[1], xor_8_out, or_2_out);
  or or_4 (or_4_out, and_8_out, and_10_out);
  D_Flip_Flop d_ff_6 (.clk(clock_1_out), .D(in_3[2]), .Q(d_ff_6_q), .en(and_2_out));  // open: Qn, preset, reset
  D_Flip_Flop d_ff_7 (.clk(clock_1_out), .D(in_3[1]), .Q(d_ff_7_q), .en(and_2_out));  // open: Qn, preset, reset
  and and_8 (and_8_out, xor_8_out, or_2_out);
  D_Flip_Flop d_ff_8 (.clk(clock_1_out), .D(in_3[0]), .Q(d_ff_8_q), .en(and_2_out));  // open: Qn, preset, reset
  xor xor_7 (xor_7_out, d_ff_2_q, d_ff_6_q);
  and and_9 (and_9_out, d_ff_2_q, d_ff_6_q);
  xor xor_8 (xor_8_out, d_ff_3_q, d_ff_7_q);
  and and_10 (and_10_out, d_ff_3_q, d_ff_7_q);
  and and_11 (A_B_3, d_ff_3_q, not_6_out);
  and and_12 (A_B_6, d_ff_2_q, not_7_out);
  xor xor_9 (xor_9_out, d_ff_8_q, ~d_ff_4_q);  // XOR_Gate
  and and_13 (and_13_out, d_ff_4_q, d_ff_8_q);
  xor xor_10 (xor_10_out, d_ff_7_q, ~d_ff_3_q);  // XOR_Gate
  and and_14 (and_14_out, d_ff_3_q, d_ff_7_q);
  not not_6 (not_6_out, d_ff_7_q);
  or or_5 (A__B, A_B_3, A_B_2);
  or or_6 (A__B_5, A_B_6, A_B_10);
  not not_7 (not_7_out, d_ff_6_q);
  xnor xnor_1 (A_B_2, d_ff_3_q, d_ff_7_q);
  xnor xnor_2 (A_B_10, d_ff_2_q, d_ff_6_q);
  and and_15 (and_15_out, xor_9_out, in_4);
  and and_16 (and_16_out, xor_10_out, or_9_out);
  not not_8 (not_8_out, d_ff_3_q);
  and and_17 (A_B_4, not_8_out, d_ff_7_q);
  or or_7 (A__B_2, A_B_2, A_B_4);
  or or_8 (A__B_6, A_B_10, A_B_7);
  and and_18 (A_B_7, not_9_out, d_ff_6_q);
  not not_9 (not_9_out, d_ff_2_q);
  xor xor_11 (out_7[0], xor_9_out, in_4);
  or or_9 (or_9_out, and_15_out, and_13_out);
  xor xor_12 (out_7[1], xor_10_out, or_9_out);
  or or_10 (or_10_out, and_16_out, and_14_out);
  xor xor_13 (out_7[3], xor_15_out, or_12_out);
  or or_11 (out_8, and_20_out, and_23_out);
  xor xor_14 (out_7[2], xor_16_out, or_10_out);
  or or_12 (or_12_out, and_21_out, and_24_out);
  not not_10 (not_10_out, d_ff_8_q);
  and and_19 (A_B_5, d_ff_4_q, not_10_out);
  and and_20 (and_20_out, xor_15_out, or_12_out);
  and and_21 (and_21_out, xor_16_out, or_10_out);
  or or_13 (A__B_3, A_B_5, A_B);
  or or_14 (A__B_7, A_B_8, A_B_11);
  and and_22 (A_B_8, d_ff_1_q, not_11_out);
  not not_11 (not_11_out, d_ff_5_q);
  xor xor_15 (xor_15_out, ~d_ff_1_q, d_ff_5_q);  // XOR_Gate
  and and_23 (and_23_out, d_ff_5_q, d_ff_1_q);
  xor xor_16 (xor_16_out, ~d_ff_2_q, d_ff_6_q);  // XOR_Gate
  and and_24 (and_24_out, d_ff_6_q, d_ff_2_q);
  xnor xnor_3 (A_B, d_ff_8_q, d_ff_4_q);
  or or_15 (A__B_4, A_B, out_20);
  xnor xnor_4 (A_B_11, d_ff_1_q, d_ff_5_q);
  not not_12 (not_12_out, d_ff_4_q);
  and and_25 (out_20, not_12_out, d_ff_8_q);
  or or_16 (A__B_8, A_B_11, A_B_9);
  and and_26 (A_B_9, not_13_out, d_ff_5_q);
  not not_13 (not_13_out, d_ff_1_q);

  // Notes on the sheet:
  //   B
  //   A
  //   A1, B1
  //   A2, B2
  //   A0, B0
  //   A3, B3
  //   A<B
endmodule
